# Fritzing sketch demo-breadboard (saved by Fritzing 0.9.3b)
breadboards: 1

parts:
  R1 = Resistor [tolerance=±5% resistance=220 package=THT]
  R2 = Resistor [tolerance=±5% resistance=220 package=THT]
  R3 = Resistor [tolerance=±5% resistance=220 package=THT]
  R4 = Resistor [tolerance=±5% resistance=220 package=THT]
  Q1 = TRANSISTOR_NPN [package=to-92-ammo]
  Q2 = TRANSISTOR_NPN [package=to-92-ammo]
  R5 = Resistor [tolerance=±5% resistance=220 package=THT]
  R6 = Resistor [tolerance=±5% resistance=220 package=THT]
  LED1 = LED - 5mm [color="Blue (430nm)" package="5 mm [THT]"]
  R7 = Resistor [tolerance=±5% resistance=220 package=THT]
  LED2 = LED - 5mm [color="Blue (430nm)" package="5 mm [THT]"]
  U1 = POT [package=3362u]  # not connected

nets:
  N1: R1.Pin_0, R3.Pin_0, R4.Pin_0, R6.Pin_1, LED2.cathode
  N2: R1.Pin_1, R2.Pin_0
  N3: R2.Pin_1, R3.Pin_1, R4.Pin_1, Q1.C, Q2.C, R7.Pin_1
  N4: Q1.E, LED1.anode
  N5: Q2.E, R5.Pin_1
  N6: R6.Pin_0, LED1.cathode
  N7: R7.Pin_0, LED2.anode
